# Fritzing sketch activity-monitor (saved by Fritzing 0.9.3b)
breadboards: 1

parts:
  Part1 = Arduino Uno (Rev3)
  GY1 = GY-521 (MPU-6050) [form="♀ (female)" package=THT]
  LED1 = LED - 5mm [color="Red (633nm)" package="5 mm [THT]"]
  LED2 = LED - 5mm [color="Green (555nm)" package="5 mm [THT]"]
  LED3 = LED - 5mm [color="Blue (430nm)" package="5 mm [THT]"]
  R1 = Resistor [tolerance=±5% resistance=220 package=THT]
  R2 = Resistor [tolerance=±5% resistance=220 package=THT]
  R3 = Resistor [tolerance=±5% resistance=220 package=THT]

nets:
  N1: Part1.A4/SDA, GY1.pin4
  N2: Part1.A5/SCL, GY1.pin3
  N3: Part1.GND, GY1.pin2, LED1.cathode, LED2.cathode, LED3.cathode
  N4: Part1.D3_PWM, R3.Pin_0
  N5: Part1.D5_PWM, R2.Pin_0
  N6: Part1.D6_PWM, R1.Pin_0
  N7: Part1.5V, GY1.pin1
  N8: LED1.anode, R3.Pin_1
  N9: LED2.anode, R2.Pin_1
  N10: LED3.anode, R1.Pin_1

custom parts:
  GY-521 (MPU-6050): Placa GY-521 basada en conjunto de acelerómetro+giroscopios MPU-6050
